// Digital circuit BW8cpu.dig as structural Verilog
module BW8cpu (
  input  VCC,
  input  GND,
  input  nRST,
  input  nIRQ,
  input  nREQ,
  input  CLK,
  output [15:0] ADDR,
  output [7:0] DATA,
  output R_nW,
  output nACK,
  output nBRK,
  output DBG
);

  wire a_dbus_a, a_dbus_l, a_lhs_a, a_rhs_a, addr_a, alu_dbus_a, alu_op, b_dbus_a, b_dbus_l, b_lhs_a,
       b_rhs_a, c_dbus_a, c_dbus_l, c_lhs_a, c_rhs_a, count, d_dbus_a, d_dbus_l, d_lhs_a, d_rhs_a, dbus_a,
       dbus_l, dec_sp, dp_addr_a, dp_dbus_a, dp_dbus_l, e_addr_a, e_xfer_l, flags, ir_dbus_l, mem_dbus_a,
       mem_dbus_l, nclk, opcode, pc_addr_a, pc_inc, pc_xfer_a, pc_xfer_l, Program_Counter_p10, reg_pc,
       reg_sp, reg_x, reg_y, sp_addr_a, sp_dec, sp_inc, sp_xfer_a, sp_xfer_l, sr_dbus_a, sr_dbus_l,
       t1_dbus_a, t1_dbus_l, t1_rhs_a, t2_dbus_a, t2_lhs_a, t_addr_a, t_inc, x_addr_a, x_dec, x_inc,
       x_xfer_a, x_xfer_l, xfer_a, xfer_l, y_addr_a, y_dec, y_inc, y_xfer_a, y_xfer_l;
  wire [7:0] dbus, lhs, reg_a, reg_b, reg_c, reg_d, reg_dp, reg_t1, reg_t2, rhs;
  wire [15:0] addr_bus, xfer;

  Reset reset_1 (.out(nRST));
  // control_unit Control_Unit: pin names not known; wires that end beside it: nIRQ, CLK, opcode, flags, nRST, nREQ, dbus_a, dbus_l, alu_op, xfer_a, xfer_l, addr_a, count, dec_sp, nBRK, nclk
  instruction_register Instruction_Register (
    .clk(CLK), .dbus(dbus), .dbus_load(ir_dbus_l), .clr(nRST));  // open: opcode
  memory_bridge Memory_Bridge (.dbus_assert(mem_dbus_a), .dbus_load(mem_dbus_l), .dbus(dbus), .mbus(DATA));
  // alu Arithmetic___Logic_Unit: pin names not known; wires that end beside it: alu_op, sr_dbus_l, sr_dbus_a, CLK, nRST, lhs, rhs, alu_dbus_a
  accumulator Accumulator (
    .addr_assert(e_addr_a), .xfer_load(e_xfer_l), .a_dbus_load(a_dbus_l), .b_dbus_load(b_dbus_l),
    .a_dbus_assert(a_dbus_a), .b_dbus_assert(b_dbus_a), .a_lhs_assert(a_lhs_a), .b_lhs_assert(b_lhs_a),
    .a_rhs_assert(a_rhs_a), .b_rhs_assert(b_rhs_a), .dbus(dbus), .xfer(xfer), .clk(CLK), .clr(nRST),
    .addr(addr_bus), .reg_a(reg_a), .reg_b(reg_b));
  general_purpose_register C_Register (
    .clk(CLK), .dbus_load(c_dbus_l), .dbus_assert(c_dbus_a), .lhs_assert(c_lhs_a), .rhs_assert(c_rhs_a),
    .clr(nRST), .dbus(dbus), .lhs(lhs), .rhs(rhs), .\reg (reg_c));
  direct_page_register DP___Temp_Register (
    .dbus(dbus), .clk(CLK), .clr(nRST), .rhs(rhs), .addr(ADDR), .assert_dp_addr(dp_addr_a),
    .assert_t1_dbus(t1_dbus_a), .assert_t1_rhs(t1_rhs_a), .assert_dp_dbus(dp_dbus_a),
    .load_t1_dbus(t1_dbus_l), .load_dp_dbus(dp_dbus_l), .load_t2_dbus(t1_dbus_l), .assert_t_addr(t_addr_a),
    .assert_t2_dbus(t2_dbus_a), .assert_t2_lhs(t2_lhs_a), .t_inc(t_inc), .reg_dp(reg_dp), .reg_t1(reg_t1),
    .reg_t2(reg_t2));
  general_purpose_register D_Register (
    .clk(CLK), .dbus_load(d_dbus_l), .dbus_assert(d_dbus_a), .lhs_assert(d_lhs_a), .rhs_assert(d_rhs_a),
    .clr(nRST), .dbus(dbus), .lhs(lhs), .rhs(rhs), .\reg (reg_d));
  // address_register Program_Counter: pin names not known; wires that end beside it: flags, dbus, xfer, CLK, nRST, pc_xfer_l, pc_addr_a, pc_xfer_a, pc_inc, Program_Counter_p10, ADDR, reg_pc
  // NotConnected on Program_Counter_p10
  // address_register Stack_Pointer: pin names not known; wires that end beside it: xfer, CLK, nRST, sp_xfer_l, sp_addr_a, sp_xfer_a, sp_inc, sp_dec, ADDR, reg_sp
  // address_register X_Index: pin names not known; wires that end beside it: xfer, CLK, nRST, x_xfer_l, x_addr_a, x_xfer_a, x_inc, x_dec, ADDR, reg_x
  // address_register Y_Index: pin names not known; wires that end beside it: xfer, CLK, nRST, y_xfer_l, y_addr_a, y_xfer_a, y_inc, y_dec, ADDR, reg_y
  // bus_controller Bus_Controller: pin names not known; wires that end beside it: dbus_a, dbus_l, xfer_a, xfer_l, addr_a, CLK, count, dec_sp, nclk, alu_dbus_a, a_dbus_a, b_dbus_a, c_dbus_a, d_dbus_a, sr_dbus_a, dp_dbus_a, t1_dbus_a, t2_dbus_a, mem_dbus_l, a_dbus_l, b_dbus_l, c_dbus_l, d_dbus_l, sr_dbus_l, dp_dbus_l

  assign DBG = 1'b1;
  assign nACK = 1'b1;
  assign R_nW = 1'b1;

  // Other names for the same wires on the sheet: mbus[7:0] = DATA

  // Notes on the sheet:
  //   External Pinout
endmodule
